// Logisim project 1921539042_MdMehdiHassanFahim_DataPath.circ as structural Verilog: 4 circuits, main circuit Datapath
module Datapath (
  input  clr,
  output [15:0] A,
  output Branch,
  output [3:0] RS,
  output [3:0] RT,
  output [15:0] B,
  output [3:0] RD,
  output [15:0] B_2,
  output Cin,
  output Zero,
  output RT___RD,
  output Cout,
  output MemoryWrite,
  output RD___IM,
  output [15:0] B_3,
  output MemoryToRegister,
  output Binv,
  output WriteEN,
  output [15:0] B_4,
  output Ramelable,
  output [2:0] ALUop,
  output SW___LW__memory_read
);

  wire and_1_out, CLK_out;
  wire [3:0] multiplexer_1_out;
  wire [15:0] adder_1_out, bit_extender_1_out, multiplexer_3_out, ram_1_data, register_1_q;
  wire [15:12] rom_1_data;

  Register #(.width(16)) register_1 (.D(multiplexer_3_out), .Q(register_1_q), .clk(CLK_out));  // open: en, clr
  Clock CLK (.out(CLK_out));
  Adder #(.width(16)) adder_1 (.a(16'h1), .b(register_1_q), .out(adder_1_out));  // open: cin, cout
  ROM #(.addrWidth(16), .dataWidth(16)) rom_1 (.addr(register_1_q), .data({rom_1_data, RS, RT, RD}));  // open: sel
  Multiplexer #(.width(4), .enable("false")) multiplexer_1 (.in0(RT), .in1(RD), .out(multiplexer_1_out), .sel(RT___RD));
  Control_unit control_unit_1 (
    .Opcode(rom_1_data), .WriteEn(WriteEN), .ALUop(ALUop), .Cin(Cin), .Binv(Binv), .RT_RD(RT___RD),
    .RD_IM(RD___IM), .Branch(Branch), .RamSelect(Ramelable), .MemWrite(MemoryWrite),
    .MemRead(SW___LW__memory_read), .MemToRegister(MemoryToRegister));
  assign bit_extender_1_out = {{12{1'b0}}, RD};  // Bit_Extender bit_extender_1
  Register_file register_file_1 (
    .Read_register_01(RS), .Write_Data(B_4), .Write_register(multiplexer_1_out), .write_enable(WriteEN),
    .Clock(CLK_out), .Read_register_02(RT), .Read_data_01(A), .Read_data_02(B), .Clear(clr));
  Multiplexer #(.width(16), .enable("false")) multiplexer_2 (
    .in0(B), .in1(bit_extender_1_out), .out(B_3), .sel(RD___IM));
  ALU alu_1 (.cin(Cin), .ALUop(ALUop), .Binv(Binv), .out_6(B_2), .Zero(Zero), .cout(Cout), .A(A), .B(B_3));
  and and_1 (and_1_out, Branch, Zero);
  Multiplexer #(.width(16), .enable("false")) multiplexer_3 (
    .in0(adder_1_out), .in1(bit_extender_1_out), .out(multiplexer_3_out), .sel(and_1_out));
  RAM #(.addrWidth(16), .dataWidth(16), .bus("separate")) ram_1 (
    .addr(B_2), .data(ram_1_data), .str(MemoryWrite), .sel(Ramelable), .clk(CLK_out),
    .ld(SW___LW__memory_read), .clr(clr));  // open: din
  Multiplexer #(.width(16), .enable("false")) multiplexer_4 (
    .in0(B_2), .in1(ram_1_data), .out(B_4), .sel(MemoryToRegister));
endmodule

module Register_file (
  input  [3:0] Read_register_01,
  input  [15:0] Write_Data,
  input  [3:0] Write_register,
  input  write_enable,
  input  Clock,
  input  Clear,
  input  [3:0] Read_register_02,
  output [15:0] Read_data_01,
  output [15:0] Read_data_02
);

  wire and_1_out, and_2_out, and_3_out, and_4_out, and_5_out, and_6_out, and_7_out, and_8_out, and_9_out,
       and_10_out, and_11_out, and_12_out, and_13_out, and_14_out, and_15_out, and_16_out, decoder_1_out0,
       decoder_1_out1, decoder_1_out2, decoder_1_out3, decoder_1_out4, decoder_1_out5, decoder_1_out6,
       decoder_1_out7, decoder_1_out8, decoder_1_out9, decoder_1_out10, decoder_1_out11, decoder_1_out12,
       decoder_1_out13, decoder_1_out14, decoder_1_out15;
  wire [15:0] R0_q, R1_q, R2_q, R3_q, R4_q, R5_q, R6_q, R7_q, R8_q, R9_q, R10_q, R11_q, R12_q, R13_q, R14_q,
       R15_q;

  Decoder #(.select(4), .enable("false")) decoder_1 (
    .out0(decoder_1_out0), .out1(decoder_1_out1), .out2(decoder_1_out2), .out3(decoder_1_out3),
    .out4(decoder_1_out4), .out5(decoder_1_out5), .out6(decoder_1_out6), .out7(decoder_1_out7),
    .out8(decoder_1_out8), .out9(decoder_1_out9), .out10(decoder_1_out10), .out11(decoder_1_out11),
    .out12(decoder_1_out12), .out13(decoder_1_out13), .out14(decoder_1_out14), .out15(decoder_1_out15),
    .sel(Write_register));
  and and_1 (and_1_out, decoder_1_out0, write_enable);
  and and_2 (and_2_out, decoder_1_out1, write_enable);
  and and_3 (and_3_out, decoder_1_out2, write_enable);
  and and_4 (and_4_out, decoder_1_out3, write_enable);
  and and_5 (and_5_out, decoder_1_out4, write_enable);
  and and_6 (and_6_out, decoder_1_out5, write_enable);
  and and_7 (and_7_out, decoder_1_out6, write_enable);
  and and_8 (and_8_out, decoder_1_out7, write_enable);
  and and_9 (and_9_out, decoder_1_out8, write_enable);
  and and_10 (and_10_out, decoder_1_out9, write_enable);
  and and_11 (and_11_out, decoder_1_out10, write_enable);
  and and_12 (and_12_out, decoder_1_out11, write_enable);
  and and_13 (and_13_out, decoder_1_out12, write_enable);
  and and_14 (and_14_out, decoder_1_out13, write_enable);
  and and_15 (and_15_out, decoder_1_out14, write_enable);
  and and_16 (and_16_out, decoder_1_out15, write_enable);
  Register #(.width(16)) R0 (.D(Write_Data), .en(and_1_out), .Q(R0_q), .clk(Clock), .clr(Clear));
  Register #(.width(16)) R1 (.D(Write_Data), .en(and_2_out), .Q(R1_q), .clk(Clock), .clr(Clear));
  Register #(.width(16)) R2 (.D(Write_Data), .en(and_3_out), .Q(R2_q), .clk(Clock), .clr(Clear));
  Register #(.width(16)) R3 (.D(Write_Data), .en(and_4_out), .Q(R3_q), .clk(Clock), .clr(Clear));
  Register #(.width(16)) R4 (.D(Write_Data), .en(and_5_out), .Q(R4_q), .clk(Clock), .clr(Clear));
  Register #(.width(16)) R5 (.D(Write_Data), .en(and_6_out), .Q(R5_q), .clk(Clock), .clr(Clear));
  Register #(.width(16)) R6 (.D(Write_Data), .en(and_7_out), .Q(R6_q), .clk(Clock), .clr(Clear));
  Register #(.width(16)) R7 (.D(Write_Data), .en(and_8_out), .Q(R7_q), .clk(Clock), .clr(Clear));
  Register #(.width(16)) R8 (.D(Write_Data), .en(and_9_out), .Q(R8_q), .clk(Clock), .clr(Clear));
  Register #(.width(16)) R9 (.D(Write_Data), .en(and_10_out), .Q(R9_q), .clk(Clock), .clr(Clear));
  Register #(.width(16)) R10 (.D(Write_Data), .en(and_11_out), .Q(R10_q), .clk(Clock), .clr(Clear));
  Register #(.width(16)) R11 (.D(Write_Data), .en(and_12_out), .Q(R11_q), .clk(Clock), .clr(Clear));
  Register #(.width(16)) R12 (.D(Write_Data), .en(and_13_out), .Q(R12_q), .clk(Clock), .clr(Clear));
  Register #(.width(16)) R13 (.D(Write_Data), .en(and_14_out), .Q(R13_q), .clk(Clock), .clr(Clear));
  Register #(.width(16)) R14 (.D(Write_Data), .en(and_15_out), .Q(R14_q), .clk(Clock), .clr(Clear));
  Register #(.width(16)) R15 (.D(Write_Data), .en(and_16_out), .Q(R15_q), .clk(Clock), .clr(Clear));
  Multiplexer #(.select(4), .width(16), .enable("false")) multiplexer_1 (
    .in0(R0_q), .in1(R1_q), .in2(R2_q), .in3(R3_q), .in4(R4_q), .in5(R5_q), .in6(R6_q), .in7(R7_q),
    .in8(R8_q), .in9(R9_q), .in10(R10_q), .in11(R11_q), .in12(R12_q), .in13(R13_q), .in14(R14_q),
    .in15(R15_q), .out(Read_data_01), .sel(Read_register_01));
  Multiplexer #(.select(4), .width(16), .enable("false")) multiplexer_2 (
    .in0(R0_q), .in1(R1_q), .in2(R2_q), .in3(R3_q), .in4(R4_q), .in5(R5_q), .in6(R6_q), .in7(R7_q),
    .in8(R8_q), .in9(R9_q), .in10(R10_q), .in11(R11_q), .in12(R12_q), .in13(R13_q), .in14(R14_q),
    .in15(R15_q), .out(Read_data_02), .sel(Read_register_02));
endmodule

module ALU (
  input  cin,
  input  [15:0] A,
  input  [15:0] B,
  input  [2:0] ALUop,
  input  Binv,
  output [15:0] out_6,
  output Zero,
  output cout
);

  wire comparator_1_lt;
  wire [3:0] bit_extender_1_out;
  wire [15:0] adder_1_out, and_1_out, bit_extender_2_out, multiplexer_1_out, not_1_out, not_2_out,
       shifter_1_out;

  assign not_1_out = ~B;  // NOT_Gate not_1, 16 bits wide
  Bit_Extender #(.in_width(16), .out_width(4)) bit_extender_1 (.in(B), .out(bit_extender_1_out));
  Multiplexer #(.width(16), .enable("false")) multiplexer_1 (
    .in0(B), .in1(not_1_out), .out(multiplexer_1_out), .sel(Binv));
  assign not_2_out = ~A;  // NOT_Gate not_2, 16 bits wide
  Comparator #(.width(16)) comparator_1 (.a(A), .b(B), .lt(comparator_1_lt));  // open: gt, eq
  assign and_1_out = A & B;  // AND_Gate and_1, 16 bits wide
  assign bit_extender_2_out = {{15{1'b0}}, comparator_1_lt};  // Bit_Extender bit_extender_2
  Shifter #(.width(16)) shifter_1 (.in(A), .\dist (bit_extender_1_out), .out(shifter_1_out));
  Adder #(.width(16)) adder_1 (.a(A), .b(multiplexer_1_out), .out(adder_1_out), .cin(cin), .cout(cout));
  Multiplexer #(.select(3), .width(16), .enable("false")) multiplexer_2 (
    .in0(and_1_out), .in1(not_2_out), .in2(adder_1_out), .in3(bit_extender_2_out), .in4(shifter_1_out),
    .out(out_6), .sel(ALUop));  // open: in5, in6, in7
  nor nor_1 (Zero, out_6[0], out_6[1], out_6[2], out_6[3], out_6[4], out_6[5], out_6[6], out_6[7], out_6[8], out_6[9], out_6[10], out_6[11], out_6[12], out_6[13], out_6[14], out_6[15]);
endmodule

module Control_unit (
  input  [3:0] Opcode,
  output WriteEn,
  output [2:0] ALUop,
  output Cin,
  output Binv,
  output RT_RD,
  output RD_IM,
  output Branch,
  output RamSelect,
  output MemWrite,
  output MemRead,
  output MemToRegister
);

  wire decoder_1_out0, decoder_1_out1, decoder_1_out2, decoder_1_out4, decoder_1_out6, decoder_1_out8,
       decoder_1_out11, decoder_1_out12, decoder_1_out13, decoder_1_out14, decoder_1_out15;

  Decoder #(.select(4), .enable("false")) decoder_1 (
    .out0(decoder_1_out0), .out1(decoder_1_out1), .out2(decoder_1_out2), .out3(MemWrite),
    .out4(decoder_1_out4), .out5(ALUop[0]), .out6(decoder_1_out6), .out7(Binv), .out8(decoder_1_out8),
    .out9(MemRead), .out10(ALUop[2]), .out11(decoder_1_out11), .out12(decoder_1_out12),
    .out13(decoder_1_out13), .out14(decoder_1_out14), .out15(decoder_1_out15), .sel(Opcode));
  or or_1 (WriteEn, decoder_1_out1, decoder_1_out2, Binv, decoder_1_out8, MemRead, ALUop[2]);
  or or_2 (RT_RD, decoder_1_out1, decoder_1_out2, ALUop[0], Binv, ALUop[2]);
  or or_3 (RD_IM, MemWrite, decoder_1_out4, decoder_1_out6, decoder_1_out8, MemRead);
  or or_4 (Branch, decoder_1_out4, decoder_1_out6);
  or or_5 (RamSelect, MemWrite, MemRead);
  or or_6 (MemToRegister, MemWrite, MemRead);
  or or_7 (ALUop[1], decoder_1_out2, MemWrite, ALUop[0], decoder_1_out6, Binv, decoder_1_out8, MemRead);

  assign Cin = Binv;
endmodule
